# Fritzing sketch how_to_connect_rotary_encoder_with_button (saved by Fritzing 0.9.3b)
breadboards: 1

parts:
  ENCODER1 = Rotary Encoder with Knob
  Bauteil1 = Arduino Mega ADK (Rev3)

nets:
  N1: ENCODER1.no_name_yet#1, Bauteil1.A0
  N2: ENCODER1.no_name_yet#2, ENCODER1.no_name_yet#4, Bauteil1.GND
  N3: ENCODER1.no_name_yet#3, Bauteil1.A1
  N4: ENCODER1.no_name_yet#5, Bauteil1.A2

custom parts:
  Rotary Encoder with Knob: Rotary Encoder with 1/4" Shaft and Knob
